# Fritzing sketch Magic 8 Ball Password Generator (saved by Fritzing 0.9.6b)

parts:
  Part1 = Arduino Nano (Rev3.0)
  U1 = LIPO-110mAh [package=lipo-110]
  Part2 = PowerBoost 500 Charger
  Grove1 = Grove OLED 128x96
  Part3 = InvenSense MPU6050
  S1 = Pushbutton [package="[THT]"]

nets:
  GND: Part1.GND, Part2.GND, Grove1.GND, Part3.GND
  N1: Part1.VIN, S1.Pin_1
  N2: Part1.A5, Grove1.SCL, Part3.SCL
  N3: Part1.A4, Grove1.SDA, Part3.SDA
  VCC: Part1.3V3, Grove1.VCC, Part3.VCC
  N4: U1.+, Part2.VBAT_IN
  N5: U1.-, Part2.GND_BAT_IN
  N6: Part2.5.0V, S1.Pin_3

notes:
  If you want to charge the battery from the Arduino Nano USB port, add wire from Arduino VUSB to LiPo VUSB.
